// Logisim project 4bit_cpu.circ as structural Verilog: 3 circuits, main circuit main
module main (
);

  wire CLK, DATA, MOV;
  wire [1:0] OP;
  wire [2:0] RD;
  wire [2:1] RA;
  wire [3:0] alu_1_o, controlled_buffer_1_out, counter_1_q, counter_1_q_2, NUM, regfile_1_out_6,
       regfile_1_out_7;
  wire [15:0] rom_1_data;
  wire [15:9] register_1_q;

  assign controlled_buffer_1_out = MOV ? NUM : 4'bz;  // Controlled_Buffer controlled_buffer_1
  Clock clock_1 (.out(CLK));
  Counter counter_1 (
    .clr(1'b0), .load(1'b0), .up(1'b1), .count(1'b1), .clk(CLK), .Q({counter_1_q_2, counter_1_q}));  // open: D, carry
  Hex_Digit_Display hex_digit_display_1 (.value(counter_1_q_2));  // open: dp
  Hex_Digit_Display hex_digit_display_2 (.value(counter_1_q));  // open: dp
  REGFILE regfile_1 (
    .INP(controlled_buffer_1_out), .C(CLK), .RA({RA, NUM[3]}), .RB(NUM[2:0]), .RD(RD),
    .out_6(regfile_1_out_6), .out_7(regfile_1_out_7));
  ROM #(.dataWidth(16)) rom_1 (.addr({counter_1_q_2, counter_1_q}), .data(rom_1_data));
  assign controlled_buffer_1_out = DATA ? alu_1_o : 4'bz;  // Controlled_Buffer controlled_buffer_2
  ALU alu_1 (.A(regfile_1_out_6), .B(regfile_1_out_7), .OP(OP), .O(alu_1_o));
  Register #(.width(16)) register_1 (
    .D(rom_1_data), .en(1'b1), .clk(CLK), .Q({register_1_q[15:14], OP, register_1_q[11:9], RA, NUM, RD}));  // open: clr
  and and_1 (MOV, register_1_q[14], register_1_q[15]);
  and and_2 (DATA, ~register_1_q[14], ~register_1_q[15]);  // AND_Gate

  // Other names for the same wires on the sheet: RB[2:0] = NUM[2:0]; RA[0] = NUM[3]

  // Notes on the sheet:
  //   contents of rom_1 (hex, n*v repeats v):
  //   c024 c02a 117 3116
endmodule

module REGFILE (
  input  [3:0] INP,
  input  C,
  input  [2:0] RA,
  input  [2:0] RB,
  input  [2:0] RD,
  output [3:0] out_6,
  output [3:0] out_7
);

  wire demultiplexer_1_out0, demultiplexer_1_out1, demultiplexer_1_out2, demultiplexer_1_out3,
       demultiplexer_1_out4, demultiplexer_1_out5, demultiplexer_1_out6, demultiplexer_1_out7;
  wire [3:0] R0_q, R1_q, R2_q, R3_q, R4_q, R5_q, R6_q, R7_q;

  Demultiplexer #(.select(3)) demultiplexer_1 (
    .out0(demultiplexer_1_out0), .out1(demultiplexer_1_out1), .out2(demultiplexer_1_out2),
    .out3(demultiplexer_1_out3), .out4(demultiplexer_1_out4), .out5(demultiplexer_1_out5),
    .out6(demultiplexer_1_out6), .out7(demultiplexer_1_out7), .in(1'b1), .sel(RD));
  Register #(.width(4)) R0 (.D(INP), .en(demultiplexer_1_out0), .clk(C), .Q(R0_q));  // open: clr
  Register #(.width(4)) R1 (.D(INP), .en(demultiplexer_1_out1), .clk(C), .Q(R1_q));  // open: clr
  Register #(.width(4)) R2 (.D(INP), .en(demultiplexer_1_out2), .clk(C), .Q(R2_q));  // open: clr
  Register #(.width(4)) R3 (.D(INP), .en(demultiplexer_1_out3), .clk(C), .Q(R3_q));  // open: clr
  Register #(.width(4)) R4 (.D(INP), .en(demultiplexer_1_out4), .clk(C), .Q(R4_q));  // open: clr
  Register #(.width(4)) R5 (.D(INP), .en(demultiplexer_1_out5), .clk(C), .Q(R5_q));  // open: clr
  Register #(.width(4)) R6 (.D(INP), .en(demultiplexer_1_out6), .clk(C), .Q(R6_q));  // open: clr
  Register #(.width(4)) R7 (.D(INP), .en(demultiplexer_1_out7), .clk(C), .Q(R7_q));  // open: clr
  Multiplexer #(.select(3), .width(4)) multiplexer_1 (
    .in0(R0_q), .in1(R1_q), .in2(R2_q), .in3(R3_q), .in4(R4_q), .in5(R5_q), .in6(R6_q), .in7(R7_q),
    .out(out_6), .sel(RA));
  Multiplexer #(.select(3), .width(4)) multiplexer_2 (
    .in0(R0_q), .in1(R1_q), .in2(R2_q), .in3(R3_q), .in4(R4_q), .in5(R5_q), .in6(R6_q), .in7(R7_q),
    .out(out_7), .sel(RB));
endmodule

module ALU (
  input  [3:0] A,
  input  [3:0] B,
  input  [1:0] OP,
  output [3:0] O
);

  wire [3:0] adder_1_out, and_1_out, or_1_out, xor_1_out;

  Adder #(.width(4)) adder_1 (.a(A), .b(B), .out(adder_1_out), .cin(1'b0));  // open: cout
  assign and_1_out = A & B;  // AND_Gate and_1, 4 bits wide
  assign or_1_out = A | B;  // OR_Gate or_1, 4 bits wide
  assign xor_1_out = A ^ B;  // XOR_Gate xor_1, 4 bits wide
  Multiplexer #(.select(2), .width(4)) multiplexer_1 (
    .in0(adder_1_out), .in1(and_1_out), .in2(or_1_out), .in3(xor_1_out), .out(O), .sel(OP));
endmodule
